// Logisim project Led7Doan.circ as structural Verilog: 1 circuit, main circuit main
module main (
  input  I0,
  input  I1,
  input  I2,
  input  I3
);

  wire D0_out, D1_out, D2_out, D3_out, D4_out, D5_out, D6_out, I1_nI0_2_out, I1_nI0_3_out, I1_nI0_out,
       I1I0_out, I2_nI0_out, I2_nI1_2_out, I2_nI1_out, I2_nI1I0_out, I2I0_out, nI1_nI0_2_out, nI1_nI0_out,
       nI2_nI0_2_out, nI2_nI0_3_out, nI2_nI0_out, nI2I1_2_out, nI2I1_out, not_1_out, not_2_out, not_3_out;

  not not_1 (not_1_out, I0);
  not not_2 (not_2_out, I1);
  not not_3 (not_3_out, I2);
  and nI2_nI0 (nI2_nI0_out, not_1_out, not_3_out);
  and nI2I1 (nI2I1_out, I1, not_3_out);
  and I1_nI0 (I1_nI0_out, not_1_out, I1);
  and I2_nI1I0 (I2_nI1I0_out, I0, not_2_out, I2);
  and nI2_nI0_2 (nI2_nI0_2_out, not_1_out, not_3_out);
  and I1_nI0_2 (I1_nI0_2_out, not_1_out, I1);
  and nI2I1_2 (nI2I1_2_out, I1, not_3_out);
  and I1_nI0_3 (I1_nI0_3_out, not_1_out, I1);
  and I2_nI1 (I2_nI1_out, not_2_out, I2);
  and nI1_nI0 (nI1_nI0_out, not_1_out, not_2_out);
  and I1I0 (I1I0_out, I0, I1);
  and nI1_nI0_2 (nI1_nI0_2_out, not_1_out, not_2_out);
  and I2_nI1_2 (I2_nI1_2_out, not_2_out, I2);
  and I2_nI0 (I2_nI0_out, not_1_out, I2);
  and nI2_nI0_3 (nI2_nI0_3_out, not_1_out, not_3_out);
  and I2I0 (I2I0_out, I0, I2);
  _7_Segment_Display u_7_segment_display_1 ();  // open: g, f, a, b, e, d, c, dp
  or D0 (D0_out, nI2_nI0_out, nI2I1_out, I1_nI0_out, I2_nI1I0_out, I3);
  or D1 (D1_out, I0, not_2_out, I2);
  or D2 (D2_out, nI2_nI0_2_out, I1_nI0_2_out);
  or D3 (D3_out, nI2I1_2_out, I1_nI0_3_out, I2_nI1_out, I3);
  or D4 (D4_out, not_3_out, nI1_nI0_out, I1I0_out);
  or D5 (D5_out, nI1_nI0_2_out, I2_nI1_2_out, I2_nI0_out, I3);
  or D6 (D6_out, nI2_nI0_3_out, I1, I2I0_out, I3);
  _7_Segment_Display u_7_segment_display_2 (
    .g(D3_out), .f(D5_out), .a(D6_out), .b(D4_out), .e(D2_out), .d(D0_out), .c(D1_out));  // open: dp

  // Notes on the sheet:
  //   I3
  //   I0
  //   ~I1
  //   ~I2
  //   I3
  //   ~I2
  //   I3
  //   I1
  //   I3
  //   D3
  //   D5
  //   D2
  //   D2
  //   D6
  //   D5
  //   D4
  //   D6
  //   D4
  //   D3
  //   D1
  //   D0
  //   D0
  //   D1
endmodule
